# Fritzing sketch Circuit_Diagram (saved by Fritzing 0.9.6b)

parts:
  Teensy1 = Teensy 4.1
  RE1 = KY-040 Rotary encoder [package=THT]
  IC1 = Hex Inverter Schmitt Trigger SN74HC14 [package="DIP (Dual Inline)"]
  C3 = Ceramic Capacitor [capacitance="100 nF" voltage=35V package="0603 [SMD, multilayer]"]
  C4 = Electrolytic Capacitor [capacitance=1µF voltage=35V package="100 mil [THT, electrolytic]"]
  C5 = Electrolytic Capacitor [capacitance=1µF voltage=35V package="100 mil [THT, electrolytic]"]
  S1 = Pushbutton [package="[SMD]"]
  C6 = Ceramic Capacitor [capacitance="100 nF" voltage=35V package="0603 [SMD, multilayer]"]
  J1 = Piezo Speaker
  R1 = Resistor [tolerance=±5% power=0.25 resistance=220 package=THT]
  R2 = Resistor [tolerance=±5% power=0.25 resistance=220 package=THT]
  LED3 = LED - 5mm [color="Green (560nm)" current=0.030 package="5 mm [THT]"]
  LED4 = LED - 5mm [color="Green (560nm)" current=0.030 package="5 mm [THT]"]
  LED5 = LED - 5mm [color="Green (560nm)" current=0.030 package="5 mm [THT]"]
  LED6 = LED - 5mm [color="Green (560nm)" current=0.030 package="5 mm [THT]"]
  R3 = Resistor [tolerance=±5% power=0.25 resistance=220 package=THT]
  R4 = Resistor [tolerance=±5% power=0.25 resistance=220 package=THT]
  LED7 = LED - 5mm [color="Red (633nm)" current=0.030 package="5 mm [THT]"]
  R5 = Resistor [tolerance=±5% power=0.25 resistance=220 package=THT]
  Part1 = LCD1602-I2C

nets:
  GND: Teensy1.GND, Teensy1.GND2, RE1.GND, IC1.GND, C3.0, C4.-, C5.-, S1.Pin_3, S1.Pin_4, C6.0, J1.pin1, LED3.cathode, LED4.cathode, LED5.cathode, LED6.cathode, LED7.cathode, Part1.GND
  N1: Teensy1.A4/D18, Part1.SDA
  N2: Teensy1.A5/D19, Part1.SCL
  VCC: Teensy1.Vin, RE1.Vcc, IC1.VCC, R5.Pin_1, Part1.VCC
  N3: Teensy1.A10/D24, IC1.1Y
  N4: Teensy1.A11/D25, RE1.DT, C5.+
  N5: Teensy1.D30, RE1.SW, C3.1
  N6: Teensy1.D32, S1.Pin_1, S1.Pin_2, C6.1
  N7: Teensy1.D33, R2.Pin_1
  N8: Teensy1.D34, R1.Pin_1
  N9: Teensy1.D35, R3.Pin_1
  N10: Teensy1.D36, R4.Pin_1
  N11: Teensy1.A15/D39, J1.pin2
  N12: RE1.CLK, IC1.1A, C4.+
  N13: R1.Pin_0, LED4.anode
  N14: R2.Pin_0, LED3.anode
  N15: LED5.anode, R3.Pin_0
  N16: LED6.anode, R4.Pin_0
  N17: LED7.anode, R5.Pin_0

custom parts:
  Teensy 4.1: The Teensy is a complete USB-based microcontoller development system, in a very small footprint, capable of implementing many types of projects. All programming is done via the USB port. No special programmer is needed, only a standard micro-USB cable and a PC or Macintosh with a USB port.
  KY-040 Rotary encoder: KY-040 Rotary Encoder with switch on breakout borad from AZ Delivery
  LCD1602-I2C: A standard character display, usually with 2x16 characters. Comes in many colors with LCM1602 IIC attached.
